# Fritzing sketch memoryGameScheme (saved by Fritzing 0.9.4)
breadboards: 1

parts:
  R1 = Resistor [tolerance=±5% resistance=220 package=THT]
  LED1 = LED - 5mm [color="Red (633nm)" package="5 mm [THT]"]
  LED2 = LED - 5mm [color="Green (555nm)" package="5 mm [THT]"]
  LED3 = LED - 5mm [color="Blue (505nm)" package="5 mm [THT]"]
  LED4 = LED - 5mm [color="Yellow (595nm)" package="5 mm [THT]"]
  R2 = Resistor [tolerance=±5% resistance=220 package=THT]
  R3 = Resistor [tolerance=±5% resistance=220 package=THT]
  R4 = Resistor [tolerance=±5% resistance=220 package=THT]
  Componente1 = Arduino Uno (Rev3)
  J1 = Piezo Speaker
  S1 = Pushbutton [package="[THT]"]
  S2 = Pushbutton [package="[THT]"]
  S3 = Pushbutton [package="[THT]"]
  S4 = Pushbutton [package="[THT]"]

nets:
  N1: R1.Pin_0, LED1.anode
  N2: R1.Pin_1, Componente1.D6_PWM
  N3: LED1.cathode, LED2.cathode, LED3.cathode, LED4.cathode, Componente1.GND, J1.pin1, S1.Pin_1, S1.Pin_2, S2.Pin_1, S2.Pin_2, S3.Pin_1, S3.Pin_2, S4.Pin_1, S4.Pin_2
  N4: LED2.anode, R2.Pin_0
  N5: LED3.anode, R3.Pin_0
  N6: LED4.anode, R4.Pin_0
  N7: R2.Pin_1, Componente1.D5_PWM
  N8: R3.Pin_1, Componente1.D4
  N9: R4.Pin_1, Componente1.D3_PWM
  N10: Componente1.D9_PWM, J1.pin2
  N11: Componente1.D10_PWM/SS, S1.Pin_3, S1.Pin_4
  N12: Componente1.D11_PWM/MOSI, S2.Pin_3, S2.Pin_4
  N13: Componente1.D12/MISO, S3.Pin_3, S3.Pin_4
  N14: Componente1.D13/SCK, S4.Pin_3, S4.Pin_4
