# Fritzing sketch PokerTexas (saved by Fritzing 0.9.10b)
breadboards: 1

parts:
  Componente1 = Arduino Uno (Rev3)
  LCD1 = LCD screen
  Componente2 = Thumb Joystick
  R1 = Trimmer Potentiometer [maximum_resistance=10kΩ knob_status=50% power=0.5W package=THT]

nets:
  N1: Componente1.A0, Componente2.VERT
  N2: Componente1.A1, Componente2.HORZ
  N3: Componente1.D8, LCD1.E
  N4: Componente1.D9_PWM, LCD1.DB4
  N5: Componente1.D10_PWM/SS, LCD1.DB5
  N6: Componente1.D11_PWM/MOSI, LCD1.DB6
  N7: Componente1.D12/MISO, LCD1.DB7
  GND: Componente1.GND, LCD1.VSS, LCD1.R/W, LCD1.LED-, Componente2.GND, R1.leg2
  N8: Componente1.D2, Componente2.SEL
  N9: Componente1.D7, LCD1.RS
  5V: Componente1.5V, LCD1.VDD, LCD1.LED+, Componente2.VCC, R1.leg1
  N10: LCD1.V0, R1.wiper

// code stored in the sketch: baraja.ino
#ifndef BARAJA_H
#define BARAJA_H


enum PALOS {DIAMANTES, TREBOLES, CORAZONES, PICAS};	//pares rojos, impares negros
enum FIGURAS {AS = 1, JOTA = 10, REINA = 11, REY = 12};	//pares rojos, impares negros


class baraja {

private:
    
public:
//	Ahora la funcion iniciar de la estructura es el constructor. 
    agrupacion_estatica() : total(0) {}

    bool anyadir(const T &p) {
        bool sePuede = this->total < MAX;
        if (sePuede) {
            this->datos[this->total] = p;
            this->total++;
        }
        return sePuede;
    }

    bool borrarUltimo() {
        bool sePuede = this->total > 0;
        if (sePuede) {
            this->total--;
        }
        return sePuede;
    }

    //Declarando la clase const_iterator (iterador constante) como friend y como
    //clase local, conseguimos que pueda haber varios iteradores, cada uno de ellos
    //llevando su propio "puntero" a que parte de la estructura estamos
    friend class const_iterator;

    class const_iterator {
    private:
        //Al separar el iterador en una clase aparte, trasladamos los miembros privados que estaban
        //en el struct a esta clase. Además, mantenemos una referencia a la agrupacion_estatica.
        int i;
        const agrupacion_estatica<T> &c;
    public:
        //Este constructor sirve como inicializador del iterador, tanto al principio como al final.
        const_iterator(const agrupacion_estatica &c_, int i_) : i(i_), c(c_) {}

        //	En la definición por defecto de los iteradores, se separa el avance del iterador
        //	a la obtención del elemento apuntado por el iterador (que en la otra implementación ocurren
        //	en la misma función.

        //Este método redefine el operador de pre-incremento (++x).
        //Representa el avance del iterador.
        const_iterator &operator++() {
            bool sePuede = this->i >= 0;
            if(sePuede){
            	i--;
            }
            return (*this);
        }

        //Este método redefine el operador de "apuntado" (*x)
        //Representa la obtención de lo apuntado por el iterador.
        const T &operator*() const {
            return(this -> c.datos[this -> i]);
        }


        //	En la definición por defecto de los iteradores, no existe la comprobación de si existe
        //	siguiente elemento. Por defecto las estructuras de datos devuelven iteradores al principio y al final,
        //	y para recorrer la estructura se compara el iterador que avanza con el iterador que apunta al final
        //	de la estructura.
        //
        bool operator!=(const const_iterator &that) const {
            return(this -> i != that.i);
        }

    };

    //Observa como nuestra agrupacion_estatica permite generar dos iteradores: uno al principio y otro al final.
    //El iterador que apunta al final de la agrupación se mantiene en este caso únicamente para hacer
    //la comprobación de que "existe siguiente".
    //Date cuenta que los valores que le pasamos como índice del iterador son para que se recorra la
    //estructura desde el último elemento (this->total - 1) hasta el primero (0).
    const_iterator begin() const { return const_iterator(*this, this->total - 1); }

    const_iterator end() const { return const_iterator(*this, -1); }
};

#endif //fin de agrupacion_estatica.h

// code stored in the sketch: mainControlers.ino
//www.elegoo.com
//2016.12.9

/*
  LiquidCrystal Library - Hello World

 Demonstrates the use a 16x2 LCD display.  The LiquidCrystal
 library works with all LCD displays that are compatible with the
 Hitachi HD44780 driver. There are many of them out there, and you
 can usually tell them by the 16-pin interface.

 This sketch prints "Hello World!" to the LCD
 and shows the time.

  The circuit:
 * LCD RS pin to digital pin 7
 * LCD Enable pin to digital pin 8
 * LCD D4 pin to digital pin 9
 * LCD D5 pin to digital pin 10
 * LCD D6 pin to digital pin 11
 * LCD D7 pin to digital pin 12
 * LCD R/W pin to ground
 * LCD VSS pin to ground
 * LCD VCC pin to 5V
 * 10K resistor:
 * ends to +5V and ground
 * wiper to LCD VO pin (pin 3)

 Library originally added 18 Apr 2008
 by David A. Mellis
 library modified 5 Jul 2009
 by Limor Fried (http://www.ladyada.net)
 example added 9 Jul 2009
 by Tom Igoe
 modified 22 Nov 2010
 by Tom Igoe

 This example code is in the public domain.

 http://www.arduino.cc/en/Tutorial/LiquidCrystal
 */

// include the library code:
#include <LiquidCrystal.h>

// initialize the library with the numbers of the interface pins
LiquidCrystal lcd(7, 8, 9, 10, 11, 12);

void setup() {
  //reset cursor for update
  lcd.setCursor(0, 0);
  // set up the LCD's number of columns and rows:
  lcd.begin(16, 2);
  // Print a message to the LCD.
  lcd.print("Hello!");
}

void loop() {
  // set the cursor to column 0, line 1
  // (note: line 1 is the second row, since counting begins with 0):
  lcd.setCursor(0, 1);
  // print the number of seconds since reset:
  lcd.print(millis() / 1000);
}
