# Fritzing sketch basicSchematic (saved by Fritzing 0.9.4)

parts:
  Componente1 = Arduino Uno (Rev3)
  IR1 = TSOP312.., 314.. [package=THT]

nets:
  N1: Componente1.D11_PWM/MOSI, IR1.Data
  N2: Componente1.5V, IR1.Vs
  GND: Componente1.GND, IR1.GND
